// Logisim project cpu.circ as structural Verilog: 2 circuits, main circuit main
module main (
  input  [31:0] INSTRUCTION,
  input  CLOCK,
  output [31:0] FETCH_ADDRESS,
  output [31:0] ra,
  output [31:0] sp,
  output [31:0] t0,
  output [31:0] t1,
  output [31:0] t2,
  output [31:0] s0,
  output [31:0] s1,
  output [31:0] a0
);

  wire undriven;
  wire [31:0] adder_1_out, Arithmetic_Logic_Unit_result, RegFile_read_data_1, RegFile_read_data_2;

  Adder #(.width(32)) adder_1 (.a(FETCH_ADDRESS), .b(32'h1), .out(adder_1_out));  // open: cin, cout
  Register #(.width(32)) PC (.D(adder_1_out), .clk(CLOCK), .Q(FETCH_ADDRESS));  // open: en, clr
  Controllogic controllogic_1 ();  // open: in_1
  Multiplexer #(.width(25), .enable("false")) multiplexer_1 (
    .in0(INSTRUCTION[31:7]), .sel(undriven));  // open: in1, out
  regfile_main RegFile (
    .rs2(INSTRUCTION[24:20]), .rd(INSTRUCTION[11:7]), .Read_Data_1(RegFile_read_data_1),
    .Read_Data_2(RegFile_read_data_2), .ra(ra), .sp(sp), .t0(t0), .t1(t1), .t2(t2), .s0(s0), .s1(s1),
    .a0(a0), .rs1(INSTRUCTION[19:15]), .Write_Data(Arithmetic_Logic_Unit_result), .clk(CLOCK));  // open: RegWEn
  alu Arithmetic_Logic_Unit (
    .A(RegFile_read_data_1), .B(RegFile_read_data_2), .Result(Arithmetic_Logic_Unit_result));  // open: ALUSel
  // mem_main DMEM: pin names not known

  // Other names for the same wires on the sheet: clk = CLOCK; fetch_addr[31:0] = FETCH_ADDRESS;
  //   rd[4:0] = INSTRUCTION[11:7]; rs1[4:0] = INSTRUCTION[19:15]; rs2[4:0] = INSTRUCTION[24:20]

  // Notes on the sheet:
  //   Output
  //   Inputs/Outputs from run.circ. DO NOT MOVE THESE.
  //   Inputs
  //   It is OK to move the PC, RegFile, ALU, and MEM to wherever is most convenient for you when constructing your CPU, and to delete this text
  //   Inputs/Outputs from run.circ. DO NOT MOVE THESE.
endmodule

module Controllogic (
  input  [31:0] in_1
);

  wire add, addi, and1, and_1_out, and_2_out, and_3_out, and_4_out, and_5_out, and_6_out, and_7_out,
       and_8_out, and_22_out, and_23_out, andi, beq, blt, bltu, bne, comparator_1_eq, comparator_2_eq,
       comparator_3_eq, comparator_4_eq, comparator_5_eq, comparator_6_eq, comparator_7_eq, comparator_8_eq,
       comparator_9_eq, comparator_10_eq, comparator_11_eq, comparator_12_eq, comparator_13_eq,
       comparator_14_eq, comparator_15_eq, comparator_16_eq, comparator_17_eq, comparator_18_eq,
       comparator_19_eq, comparator_20_eq, comparator_21_eq, comparator_22_eq, comparator_23_eq,
       comparator_24_eq, comparator_25_eq, comparator_26_eq, comparator_27_eq, comparator_28_eq,
       comparator_29_eq, comparator_30_eq, comparator_31_eq, divu, jal, jalr, lb, lh, lui, lw, mul, mulh,
       mulhu, or1, ori, remu, sll1, slli, slt, slti, srai, srl1, srli, sub, sw, xor1, xori;

  Comparator #(.width(7)) comparator_1 (.a(in_1[6:0]), .b(7'b0110011), .eq(comparator_1_eq));  // open: gt, lt
  Comparator #(.width(3)) comparator_2 (.a(in_1[14:12]), .b(3'b000), .eq(comparator_2_eq));  // open: gt, lt
  Comparator #(.width(3)) comparator_3 (.a(in_1[14:12]), .b(3'b001), .eq(comparator_3_eq));  // open: gt, lt
  Comparator #(.width(3)) comparator_4 (.a(in_1[14:12]), .b(3'b010), .eq(comparator_4_eq));  // open: gt, lt
  Comparator #(.width(3)) comparator_5 (.a(in_1[14:12]), .b(3'b011), .eq(comparator_5_eq));  // open: gt, lt
  Comparator #(.width(3)) comparator_6 (.a(in_1[14:12]), .b(3'b100), .eq(comparator_6_eq));  // open: gt, lt
  Comparator #(.width(3)) comparator_7 (.a(in_1[14:12]), .b(3'b101), .eq(comparator_7_eq));  // open: gt, lt
  Comparator #(.width(3)) comparator_8 (.a(in_1[14:12]), .b(3'b110), .eq(comparator_8_eq));  // open: gt, lt
  Comparator #(.width(3)) comparator_9 (.a(in_1[14:12]), .b(3'b111), .eq(comparator_9_eq));  // open: gt, lt
  and and_1 (and_1_out, comparator_1_eq, comparator_3_eq);
  and and_2 (and_2_out, comparator_1_eq, comparator_4_eq);
  and and_3 (and_3_out, comparator_1_eq, comparator_5_eq);
  and and_4 (and_4_out, comparator_1_eq, comparator_6_eq);
  and and_5 (and_5_out, comparator_1_eq, comparator_7_eq);
  and and_6 (and_6_out, comparator_1_eq, comparator_8_eq);
  and and_7 (and_7_out, comparator_1_eq, comparator_9_eq);
  and and_8 (and_8_out, comparator_1_eq, comparator_2_eq);
  Comparator #(.width(7)) comparator_10 (.a(in_1[31:25]), .b({7{1'b0}}), .eq(comparator_10_eq));  // open: gt, lt
  Comparator #(.width(7)) comparator_11 (.a(in_1[31:25]), .b(7'b0000001), .eq(comparator_11_eq));  // open: gt, lt
  Comparator #(.width(7)) comparator_12 (.a(in_1[31:25]), .b(7'b0100000), .eq(comparator_12_eq));  // open: gt, lt
  and and_9 (add, and_8_out, comparator_10_eq);
  and and_10 (mul, and_8_out, comparator_11_eq);
  and and_11 (sub, and_8_out, comparator_12_eq);
  and and_12 (sll1, and_1_out, comparator_10_eq);
  and and_13 (mulh, and_1_out, comparator_11_eq);
  and and_14 (slt, comparator_10_eq, and_2_out);
  and and_15 (mulhu, comparator_11_eq, and_3_out);
  and and_16 (xor1, comparator_10_eq, and_4_out);
  and and_17 (divu, comparator_11_eq, and_5_out);
  and and_18 (srl1, comparator_10_eq, and_5_out);
  and and_19 (or1, comparator_10_eq, and_6_out);
  and and_20 (remu, comparator_11_eq, and_7_out);
  and and_21 (and1, comparator_10_eq, and_7_out);
  Comparator #(.width(7)) comparator_13 (.a(in_1[6:0]), .b(7'b0000011), .eq(comparator_13_eq));  // open: gt, lt
  Comparator #(.width(7)) comparator_14 (.a(in_1[6:0]), .b(7'b0010011), .eq(comparator_14_eq));  // open: gt, lt
  Comparator #(.width(3)) comparator_15 (.a(in_1[14:12]), .b(3'b000), .eq(comparator_15_eq));  // open: gt, lt
  Comparator #(.width(3)) comparator_16 (.a(in_1[14:12]), .b(3'b001), .eq(comparator_16_eq));  // open: gt, lt
  Comparator #(.width(3)) comparator_17 (.a(in_1[14:12]), .b(3'b010), .eq(comparator_17_eq));  // open: gt, lt
  Comparator #(.width(3)) comparator_18 (.a(in_1[14:12]), .b(3'b100), .eq(comparator_18_eq));  // open: gt, lt
  Comparator #(.width(3)) comparator_19 (.a(in_1[14:12]), .b(3'b101), .eq(comparator_19_eq));  // open: gt, lt
  Comparator #(.width(3)) comparator_20 (.a(in_1[14:12]), .b(3'b110), .eq(comparator_20_eq));  // open: gt, lt
  Comparator #(.width(3)) comparator_21 (.a(in_1[14:12]), .b(3'b111), .eq(comparator_21_eq));  // open: gt, lt
  Comparator #(.width(7)) comparator_22 (.a(in_1[31:25]), .b({7{1'b0}}), .eq(comparator_22_eq));  // open: gt, lt
  Comparator #(.width(7)) comparator_23 (.a(in_1[31:25]), .b(7'b0100000), .eq(comparator_23_eq));  // open: gt, lt
  Comparator #(.width(7)) comparator_24 (.a(in_1[6:0]), .b(7'b1100111), .eq(comparator_24_eq));  // open: gt, lt
  and and_22 (and_22_out, comparator_14_eq, comparator_16_eq);
  and and_23 (and_23_out, comparator_14_eq, comparator_19_eq);
  and and_24 (lb, comparator_13_eq, comparator_15_eq);
  and and_25 (lh, comparator_13_eq, comparator_16_eq);
  and and_26 (lw, comparator_13_eq, comparator_17_eq);
  and and_27 (addi, comparator_14_eq, comparator_15_eq);
  and and_28 (slli, and_22_out, comparator_22_eq);
  and and_29 (slti, comparator_14_eq, comparator_17_eq);
  and and_30 (xori, comparator_14_eq, comparator_18_eq);
  and and_31 (srli, and_23_out, comparator_22_eq);
  and and_32 (srai, and_23_out, comparator_23_eq);
  and and_33 (ori, comparator_14_eq, comparator_20_eq);
  and and_34 (andi, comparator_14_eq, comparator_21_eq);
  and and_35 (jalr, comparator_15_eq, comparator_24_eq);
  Comparator #(.width(7)) comparator_25 (.a(in_1[6:0]), .b(7'b0100011), .eq(comparator_25_eq));  // open: gt, lt
  Comparator #(.width(3)) comparator_26 (.a(in_1[14:12]), .b(3'b010), .eq(comparator_26_eq));  // open: gt, lt
  Comparator #(.width(7)) comparator_27 (.a(in_1[6:0]), .b(7'b1100011), .eq(comparator_27_eq));  // open: gt, lt
  Comparator #(.width(3)) comparator_28 (.a(in_1[14:12]), .b(3'b000), .eq(comparator_28_eq));  // open: gt, lt
  Comparator #(.width(3)) comparator_29 (.a(in_1[14:12]), .b(3'b100), .eq(comparator_29_eq));  // open: gt, lt
  Comparator #(.width(3)) comparator_30 (.a(in_1[14:12]), .b(3'b110), .eq(comparator_30_eq));  // open: gt, lt
  Comparator #(.width(3)) comparator_31 (.a(in_1[14:12]), .b(3'b001), .eq(comparator_31_eq));  // open: gt, lt
  Comparator #(.width(7)) comparator_32 (.a(in_1[6:0]), .b(7'b0110111), .eq(lui));  // open: gt, lt
  Comparator #(.width(7)) comparator_33 (.a(in_1[6:0]), .b(7'b1101111), .eq(jal));  // open: gt, lt
  and and_36 (sw, comparator_25_eq, comparator_26_eq);
  and and_37 (beq, comparator_27_eq, comparator_28_eq);
  and and_38 (blt, comparator_27_eq, comparator_29_eq);
  and and_39 (bltu, comparator_27_eq, comparator_30_eq);
  and and_40 (bne, comparator_27_eq, comparator_31_eq);

  // Other names for the same wires on the sheet: INSTRUCTION[31:0] = in_1; Opcode[6:0] = in_1[6:0];
  //   funct3[2:0] = in_1[14:12]; funct7[6:0] = in_1[31:25]

  // Notes on the sheet:
  //   R-type Instructions
  //   compare opcode
  //   compare funct3
  //   compare funct7
  //   compare opcode
  //   compare funct3
  //   compare funct7
  //   I-type Instructions
  //   compare opcode
  //   compare funct3
  //   compare opcode
  //   compare funct3
  //   compare opcode
  //   compare opcode
  //   S-type Instruction
  //   SB-type Instructions
  //   U-type Instruction
  //   UJ-type Instruction
endmodule
